// Logisim project 0.Logisim implementation.circ as structural Verilog: 1 circuit, main circuit main
module main (
  input  S4,
  input  S3,
  input  S2,
  input  S1,
  input  S0,
  input  S1_2,
  input  Enable__Active_Low,
  input  Selector
);

  wire Clk_out, not_1_out, not_2_out;
  wire [6:0] multiplexer_1_out, multiplexer_2_out, multiplexer_3_out, multiplexer_4_out, multiplexer_5_out,
       multiplexer_6_out, multiplexer_7_out, register_1_q, register_2_q, register_3_q, register_4_q,
       register_5_q, register_6_q, register_7_q, register_8_q, register_9_q, register_10_q, register_11_q,
       register_12_q, rom_1_data;

  ROM #(.addrWidth(5), .dataWidth(7)) rom_1 (.addr({S4, S3, S2, S1, S0}), .data(rom_1_data));  // open: sel
  not not_1 (not_1_out, S1_2);
  Register #(.width(7)) register_1 (
    .D(rom_1_data), .Q(register_1_q), .clk(Clk_out), .clr(Enable__Active_Low));  // open: en
  Register #(.width(7)) register_2 (
    .D(register_3_q), .Q(register_2_q), .clk(Clk_out), .clr(Enable__Active_Low));  // open: en
  Register #(.width(7)) register_3 (
    .D(register_1_q), .Q(register_3_q), .clk(Clk_out), .clr(Enable__Active_Low));  // open: en
  Register #(.width(7)) register_4 (
    .D(register_2_q), .Q(register_4_q), .clk(Clk_out), .clr(Enable__Active_Low));  // open: en
  Register #(.width(7)) register_5 (
    .D(register_4_q), .Q(register_5_q), .clk(Clk_out), .clr(Enable__Active_Low));  // open: en
  Multiplexer #(.width(7)) multiplexer_1 (
    .in0(register_6_q), .in1(register_12_q), .out(multiplexer_1_out), .sel(S1_2), .en(not_2_out));
  Register #(.width(7)) register_6 (
    .D(register_5_q), .Q(register_6_q), .clk(Clk_out), .clr(Enable__Active_Low));  // open: en
  Multiplexer #(.width(7)) multiplexer_2 (
    .in0(multiplexer_1_out), .in1(register_8_q), .out(multiplexer_2_out), .sel(Selector), .en(not_2_out));
  Multiplexer #(.width(7)) multiplexer_3 (
    .in0(register_7_q), .in1(register_9_q), .out(multiplexer_3_out), .sel(Selector), .en(not_2_out));
  Multiplexer #(.width(7)) multiplexer_4 (
    .in0(register_8_q), .in1(register_10_q), .out(multiplexer_4_out), .sel(Selector), .en(not_2_out));
  Multiplexer #(.width(7)) multiplexer_5 (
    .in0(register_9_q), .in1(register_11_q), .out(multiplexer_5_out), .sel(Selector), .en(not_2_out));
  Multiplexer #(.width(7)) multiplexer_6 (
    .in0(register_10_q), .in1(register_12_q), .out(multiplexer_6_out), .sel(Selector), .en(not_2_out));
  Multiplexer #(.width(7)) multiplexer_7 (
    .in0(register_11_q), .in1(register_7_q), .out(multiplexer_7_out), .sel(Selector), .en(not_2_out));
  not not_2 (not_2_out, Enable__Active_Low);
  Register #(.width(7)) register_7 (
    .D(multiplexer_2_out), .Q(register_7_q), .clk(Clk_out), .clr(Enable__Active_Low));  // open: en
  Register #(.width(7)) register_8 (
    .D(multiplexer_3_out), .Q(register_8_q), .clk(Clk_out), .clr(Enable__Active_Low));  // open: en
  Register #(.width(7)) register_9 (
    .D(multiplexer_4_out), .Q(register_9_q), .clk(Clk_out), .clr(Enable__Active_Low));  // open: en
  Register #(.width(7)) register_10 (
    .D(multiplexer_5_out), .Q(register_10_q), .clk(Clk_out), .clr(Enable__Active_Low));  // open: en
  Register #(.width(7)) register_11 (
    .D(multiplexer_6_out), .Q(register_11_q), .clk(Clk_out), .clr(Enable__Active_Low));  // open: en
  Register #(.width(7)) register_12 (
    .D(multiplexer_7_out), .Q(register_12_q), .clk(Clk_out), .clr(Enable__Active_Low));  // open: en
  _7_Segment_Display u_7_segment_display_1 (
    .g(register_12_q[3]), .f(register_12_q[4]), .a(register_12_q[5]), .b(register_12_q[6]),
    .e(register_12_q[2]), .d(register_12_q[1]), .c(register_12_q[0]), .dp(not_1_out));
  Clock Clk (.out(Clk_out));
  _7_Segment_Display u_7_segment_display_2 (
    .g(register_11_q[3]), .f(register_11_q[4]), .a(register_11_q[5]), .b(register_11_q[6]),
    .e(register_11_q[2]), .d(register_11_q[1]), .c(register_11_q[0]), .dp(not_1_out));
  _7_Segment_Display u_7_segment_display_3 (
    .g(register_10_q[3]), .f(register_10_q[4]), .a(register_10_q[5]), .b(register_10_q[6]),
    .e(register_10_q[2]), .d(register_10_q[1]), .c(register_10_q[0]), .dp(not_1_out));
  _7_Segment_Display u_7_segment_display_4 (
    .g(register_9_q[3]), .f(register_9_q[4]), .a(register_9_q[5]), .b(register_9_q[6]), .e(register_9_q[2]),
    .d(register_9_q[1]), .c(register_9_q[0]), .dp(not_1_out));
  _7_Segment_Display u_7_segment_display_5 (
    .g(register_8_q[3]), .f(register_8_q[4]), .a(register_8_q[5]), .b(register_8_q[6]), .e(register_8_q[2]),
    .d(register_8_q[1]), .c(register_8_q[0]), .dp(not_1_out));
  _7_Segment_Display u_7_segment_display_6 (
    .g(register_7_q[3]), .f(register_7_q[4]), .a(register_7_q[5]), .b(register_7_q[6]), .e(register_7_q[2]),
    .d(register_7_q[1]), .c(register_7_q[0]), .dp(not_1_out));

  // Notes on the sheet:
  //   contents of rom_1 (hex, n*v repeats v):
  //   77 41 6e 6b 59 3f 61 7f 7b 7d 36 3e 3c 5d 16 7c 3b 57 1f e 4f 1d d f c 1e 7 5*2
  //   Selector = 0 : scroll right to left
  //   Selector = 1 : scroll  left to right
endmodule
